// Logisim project 14bce110_fetchdecode (1).circ as structural Verilog: 1 circuit, main circuit main
// T1
module main (
  output I,
  output [2:0] out_2,
  output [11:0] out_3
);

  wire and_1_out, and_2_out, clock_1_out, clock_2_out, FGI_q, T1_out, xor_1_out;
  wire [11:0] adder_1_out, AR_q, multiplexer_1_out, multiplexer_2_out, multiplexer_3_out, PC_q, register_1_q;
  wire [15:0] AC_q, adder_2_out, and_3_out, DR_q, multiplexer_4_out, ram_1_data;

  Multiplexer #(.width(12), .enable("false")) multiplexer_1 (
    .in0(register_1_q), .in1(register_1_q), .out(multiplexer_1_out), .sel(FGI_q));
  Clock T1 (.out(T1_out));
  Register #(.width(12)) PC (.D(multiplexer_2_out), .Q(PC_q), .clk(T1_out));  // open: en, clr
  Multiplexer #(.width(12), .enable("false")) multiplexer_2 (
    .in0(multiplexer_1_out), .in1(AR_q), .out(multiplexer_2_out), .sel(out_2[2]));
  Multiplexer #(.width(12), .enable("false")) multiplexer_3 (
    .in0(PC_q), .in1(out_3), .out(multiplexer_3_out), .sel(and_1_out));
  Adder #(.width(12)) adder_1 (.a(PC_q), .b({12{1'b0}}), .out(adder_1_out), .cin(1'b1));  // open: cout
  Register #(.width(12)) AR (.D(multiplexer_3_out), .Q(AR_q), .clk(T1_out));  // open: en, clr
  Register #(.width(12)) register_1 (.D(adder_1_out), .Q(register_1_q), .clk(T1_out));  // open: en, clr
  RAM #(.addrWidth(12), .dataWidth(16)) ram_1 (.addr(AR_q), .data(ram_1_data), .clk(T1_out));  // open: sel, ld, clr
  Clock clock_1 (.out(clock_1_out));
  and and_1 (and_1_out, clock_1_out, xor_1_out);
  Register #(.width(16)) IR (.D(ram_1_data), .Q({I, out_2, out_3}), .clk(T1_out));  // open: en, clr
  xor xor_1 (xor_1_out, 1'b0, I);
  Multiplexer #(.select(3), .width(16), .enable("false")) multiplexer_4 (
    .in0(and_3_out), .in1(adder_2_out), .out(multiplexer_4_out), .sel(out_2));  // open: in2, in3, in4, in5, in6, in7
  and and_2 (and_2_out, out_3[9], out_2[0], out_2[1], out_2[2], I);
  Register #(.width(16)) AC (.D(multiplexer_4_out), .Q(AC_q), .clk(clock_2_out));  // open: en, clr
  Clock clock_2 (.out(clock_2_out));
  assign and_3_out = AC_q & DR_q;  // AND_Gate and_3, 16 bits wide
  Register #(.width(16)) DR (.D({4'b0000, out_3}), .Q(DR_q), .clk(T1_out));  // open: en, clr
  Adder #(.width(16)) adder_2 (.a(AC_q), .b(DR_q), .out(adder_2_out));  // open: cin, cout
  D_Flip_Flop FGI (.clk(T1_out), .Q(FGI_q), .en(and_2_out));  // open: D, Qn, preset, reset
  Register register_2 ();  // open: D, en, Q, clk, clr

  // Notes on the sheet:
  //   Fetch Unit
endmodule
