// Logisim project 14bce110_fetchunit.circ as structural Verilog: 1 circuit, main circuit main
// T1
module main (
  output I,
  output [2:0] OPCODE,
  output [11:0] Instruction_Code
);

  wire T1_out, T2_out;
  wire [11:0] adder_1_out, AR_q, PC_q, register_1_q;
  wire [15:0] ram_1_data;

  Clock T1 (.out(T1_out));
  Register #(.width(12)) PC (.D(register_1_q), .Q(PC_q), .clk(T1_out));  // open: en, clr
  Clock T2 (.out(T2_out));
  Register #(.width(12)) AR (.D(PC_q), .Q(AR_q), .clk(T1_out));  // open: en, clr
  Adder #(.width(12)) adder_1 (.a(PC_q), .b({12{1'b0}}), .out(adder_1_out), .cin(1'b1));  // open: cout
  Register #(.width(12)) register_1 (.D(adder_1_out), .Q(register_1_q), .clk(T2_out));  // open: en, clr
  RAM #(.addrWidth(12), .dataWidth(16)) ram_1 (.addr(AR_q), .data(ram_1_data), .clk(T2_out));  // open: sel, ld, clr
  Register #(.width(16)) IR (.D(ram_1_data), .Q({I, OPCODE, Instruction_Code}), .clk(T2_out));  // open: en, clr

  // Notes on the sheet:
  //   Fetch Unit
endmodule
