// Logisim project Booths Algorithm.circ as structural Verilog: 2 circuits, main circuit main
module main (
  input  in_1
);

  wire clock_1_out, decoder_1_out0, not_1_out, Q_2_out;
  wire [1:0] d_ff_1_q;
  wire [2:0] SC_q;
  wire [4:0] A_q4, adder_1_out, B_q, multiplexer_1_out, Q_q, subtractor_1_out;

  Counter #(.width(3), .max('h5)) SC (.Q(SC_q), .clk(clock_1_out));  // open: load, D, count, carry, clr
  Clock clock_1 (.out(clock_1_out));
  Decoder #(.select(3)) decoder_1 (
    .out0(decoder_1_out0), .sel(SC_q));  // open: out1, out2, out3, out4, out5, out6, out7, en
  Subtractor #(.width(5)) subtractor_1 (.a(A_q4), .b(B_q), .out(subtractor_1_out));  // open: bin, bout
  Adder #(.width(5)) adder_1 (.a(A_q4), .b(B_q), .out(adder_1_out));  // open: cin, cout
  Multiplexer #(.select(2), .width(5)) multiplexer_1 (
    .in0(A_q4), .in1(adder_1_out), .in2(subtractor_1_out), .in3(A_q4), .out(multiplexer_1_out), .sel(d_ff_1_q));  // open: en
  Register #(.width(5)) B (.Q(B_q));  // open: D, en, clk, clr
  not not_1 (not_1_out, decoder_1_out0);
  Shift_Register #(.length(5)) A (
    .shift(not_1_out), .in(A_q4[4]), .clk(clock_1_out), .load(clock_1_out), .clr(decoder_1_out0),
    .d0(multiplexer_1_out[4]), .q0(A_q4[4]), .d1(multiplexer_1_out[4]), .q1(A_q4[3]),
    .d2(multiplexer_1_out[3]), .q2(A_q4[2]), .d3(multiplexer_1_out[2]), .q3(A_q4[1]),
    .d4(multiplexer_1_out[1]), .q4(A_q4[0]));  // open: out
  Register #(.width(5)) Q (.Q(Q_q));  // open: D, en, clk, clr
  Shift_Register #(.length(5)) Q_2 (
    .shift(not_1_out), .in(multiplexer_1_out[0]), .clk(clock_1_out), .out(Q_2_out), .load(decoder_1_out0),
    .clr(in_1), .d0(Q_q[4]), .d1(Q_q[3]), .d2(Q_q[2]), .d3(Q_q[1]), .d4(Q_q[0]), .q4(d_ff_1_q[1]));  // open: q0, q1, q2, q3
  D_Flip_Flop d_ff_1 (.clk(clock_1_out), .D(Q_2_out), .Q(d_ff_1_q[0]), .reset(in_1));  // open: Qn, preset, en
endmodule

module Buf (
  input  in_1,
  output out_2
);

  wire buffer_1_out, buffer_2_out, buffer_3_out, buffer_4_out, buffer_5_out, buffer_6_out, buffer_7_out;

  buf buffer_1 (buffer_1_out, in_1);
  buf buffer_2 (buffer_2_out, buffer_1_out);
  buf buffer_3 (buffer_3_out, buffer_2_out);
  buf buffer_4 (buffer_4_out, buffer_3_out);
  buf buffer_5 (buffer_5_out, buffer_4_out);
  buf buffer_6 (buffer_6_out, buffer_7_out);
  buf buffer_7 (buffer_7_out, buffer_5_out);
  buf buffer_8 (out_2, buffer_6_out);
endmodule
