// Logisim project Multiply_14bce105.circ as structural Verilog: 1 circuit, main circuit main
module main (
  input  [7:0] in_1,
  input  [4:0] in_2,
  input  [2:0] in_3,
  input  [2:0] in_4
);

  wire clock_1_out, register_3_q;
  wire [2:0] adder_2_out, counter_1_q;
  wire [7:0] adder_1_out, multiplexer_1_out, register_2_q, shifter_1_out;
  wire [16:0] register_1_q;
  wire [16:8] shifter_1_out_2;

  Clock clock_1 (.out(clock_1_out));
  Register register_1 (.D(shifter_1_out), .Q(register_1_q[7:0]), .clk(clock_1_out));  // open: en, clr
  Register register_2 (.D(shifter_1_out_2[15:8]), .Q(register_2_q), .clk(clock_1_out));  // open: en, clr
  buf buffer_1 (register_1_q[16], register_3_q);
  Register #(.width(1)) register_3 (.D(shifter_1_out_2[16]), .Q(register_3_q), .clk(clock_1_out));  // open: en, clr
  Comparator #(.width(3)) comparator_1 (.a(counter_1_q), .b(in_4), .eq(register_3_q));  // open: gt, lt
  Adder adder_1 (.a(in_1), .b(register_2_q), .out(adder_1_out), .cout(shifter_1_out_2[16]));  // open: cin
  Multiplexer #(.width(8)) multiplexer_1 (
    .in0(register_1_q[7:0]), .in1(adder_1_out), .out(multiplexer_1_out), .sel(register_1_q[0]));  // open: en
  Shifter #(.width(17), .shift("lr")) shifter_1 (
    .in({register_1_q[16], multiplexer_1_out, register_1_q[7:0]}), .\dist (in_2),
    .out({shifter_1_out_2, shifter_1_out}));
  Counter #(.width(3), .max('h7)) counter_1 (
    .D(adder_2_out), .Q(counter_1_q), .clk(clock_1_out));  // open: load, count, carry, clr
  Adder #(.width(3)) adder_2 (.a(counter_1_q), .b(in_3), .out(adder_2_out));  // open: cin, cout

  // Notes on the sheet:
  //       Q
  //           B
  //   A
  //   E
  //   SC
endmodule
