// Logisim project SimpleMultiplication.circ as structural Verilog: 1 circuit, main circuit main
module main (
  input  in_1,
  input  in_2,
  input  [3:0] in_3,
  input  in_4,
  input  in_5,
  output [7:0] out_6,
  output [7:0] out_7,
  output [7:0] out_8
);

  wire and_1_out, clock_1_out, comparator_1_eq, not_1_out;
  wire [3:0] counter_1_q;
  wire [7:0] adder_1_cout, register_2_q;
  wire [7:7] multiplexer_1_out;

  Comparator #(.width(4)) comparator_1 (.a(in_3), .b(counter_1_q), .eq(comparator_1_eq));  // open: gt, lt
  not not_1 (not_1_out, comparator_1_eq);
  Clock clock_1 (.out(clock_1_out));
  Register register_1 (.D(adder_1_cout), .Q(out_6), .clk(and_1_out), .clr(in_1));  // open: en
  Register register_2 (.Q(register_2_q), .clk(and_1_out), .clr(in_2));  // open: D, en
  Register register_3 (.D({multiplexer_1_out[7], out_8[7:1]}), .Q(out_8), .clk(and_1_out), .clr(in_4));  // open: en
  and and_1 (and_1_out, clock_1_out, not_1_out);
  Register #(.width(1)) register_4 (.D(adder_1_cout[7]), .clk(and_1_out));  // open: en, Q, clr
  Adder adder_1 (.a(out_6), .b(register_2_q), .out(out_7), .cout(adder_1_cout[7]));  // open: cin
  Multiplexer #(.width(8), .enable("false")) multiplexer_1 (
    .in0(out_6), .in1(out_7), .out({adder_1_cout[6:0], multiplexer_1_out[7]}), .sel(out_8[0]));
  Counter #(.width(4), .max('hf), .ongoal("stay")) counter_1 (
    .count(in_5), .Q(counter_1_q), .clk(and_1_out));  // open: load, D, carry, clr

  // Notes on the sheet:
  //   A
  //   M
  //   Q
endmodule
