// Logisim project adder-subtractors using nand and nor gates.circ as structural Verilog: 1 circuit, main circuit main
module main (
  input  A,
  input  A_2,
  input  B,
  input  B_2,
  input  A_3,
  input  A_4,
  input  B_3,
  input  B_4,
  input  A_5,
  input  B_5,
  input  Cin,
  input  A_6,
  input  B_6,
  input  in_14,
  input  A_7,
  input  B_7,
  input  in_17,
  input  A_8,
  input  B_8,
  input  in_20,
  output Sum,
  output Sum_2,
  output Carry,
  output Carry_2,
  output Difference,
  output Difference_2,
  output Borrow,
  output Borrow_2,
  output Sum_3,
  output Carry_3,
  output Sum_4,
  output Carry_4,
  output Difference_3,
  output Borrow_3,
  output Difference_4,
  output Borrow_4
);

  wire nand_1_out, nand_2_out, nand_3_out, nand_4_out, nand_5_out, nand_6_out, nand_7_out, nand_8_out,
       nand_9_out, nand_10_out, nand_11_out, nand_12_out, nand_13_out, nand_14_out, nand_19_out, nand_20_out,
       nand_21_out, nand_22_out, nand_23_out, nand_24_out, nand_25_out, nand_26_out, nand_27_out,
       nand_28_out, nand_30_out, nand_31_out, nand_32_out, nand_34_out, nand_35_out, nand_36_out,
       nand_37_out, nor_1_out, nor_2_out, nor_3_out, nor_4_out, nor_5_out, nor_6_out, nor_7_out, nor_8_out,
       nor_9_out, nor_10_out, nor_11_out, nor_12_out, nor_13_out, nor_14_out, nor_15_out, nor_16_out,
       nor_17_out, nor_18_out, nor_19_out, nor_20_out, nor_21_out, nor_22_out, nor_23_out, nor_24_out,
       nor_25_out, nor_26_out, nor_27_out, nor_28_out, nor_29_out, nor_30_out, nor_31_out, nor_32_out,
       nor_33_out, nor_35_out, nor_36_out, nor_37_out, nor_39_out;

  nand nand_1 (nand_1_out, A_2, B);
  nand nand_2 (nand_2_out, A_4, B_3);
  nand nand_3 (nand_3_out, A_4, A_4);
  nand nand_4 (nand_4_out, A_8, B_8);
  not nand_5 (nand_5_out, A_8);  // NAND_Gate
  not nand_6 (nand_6_out, B_8);  // NAND_Gate
  not nand_7 (nand_7_out, in_20);  // NAND_Gate
  nand nand_8 (nand_8_out, A_2, nand_1_out);
  nand nand_9 (nand_9_out, nand_1_out, B, B);
  nand nand_10 (nand_10_out, A_2, B);
  nand nand_11 (nand_11_out, A_4, nand_2_out);
  nand nand_12 (nand_12_out, nand_2_out, B_3, B_3);
  nand nand_13 (nand_13_out, nand_3_out, B_3);
  nand nand_14 (nand_14_out, A_5, B_5);
  nor nor_1 (nor_1_out, A_6, B_6);
  nor nor_2 (nor_2_out, A_7, B_7);
  nand nand_15 (Sum_2, nand_8_out, nand_9_out);
  nand nand_16 (Carry, nand_10_out, nand_10_out);
  nand nand_17 (Difference_2, nand_11_out, nand_12_out);
  nand nand_18 (Borrow, nand_13_out, nand_13_out);
  nand nand_19 (nand_19_out, A_5, nand_14_out);
  nand nand_20 (nand_20_out, nand_14_out, B_5, B_5);
  nand nand_21 (nand_21_out, A_5, B_5);
  nor nor_3 (nor_3_out, A_6, nor_1_out);
  nor nor_4 (nor_4_out, nor_1_out, B_6);
  not nor_5 (nor_5_out, A_6);  // NOR_Gate
  not nor_6 (nor_6_out, B_6);  // NOR_Gate
  nand nand_22 (nand_22_out, A_8, nand_4_out);
  nand nand_23 (nand_23_out, nand_4_out, B_8, B_8);
  nand nand_24 (nand_24_out, nand_6_out, nand_7_out);
  nor nor_7 (nor_7_out, nor_3_out, nor_4_out);
  nor nor_8 (nor_8_out, A_7, nor_2_out);
  nor nor_9 (nor_9_out, nor_2_out, B_7);
  nand nand_25 (nand_25_out, nand_5_out, nand_24_out);
  nand nand_26 (nand_26_out, B_8, in_20);
  nand nand_27 (nand_27_out, nand_19_out, nand_20_out);
  nor nor_10 (nor_10_out, nor_7_out, nor_7_out);
  nor nor_11 (nor_11_out, nor_5_out, nor_6_out);
  nor nor_12 (nor_12_out, nor_8_out, nor_9_out);
  nand nand_28 (nand_28_out, nand_22_out, nand_23_out);
  nor nor_13 (nor_13_out, nor_10_out, in_14);
  nand nand_29 (Borrow_4, nand_25_out, nand_26_out);
  nor nor_14 (nor_14_out, A, B_2);
  nor nor_15 (nor_15_out, A_3, B_4);
  nand nand_30 (nand_30_out, nand_27_out, Cin);
  nand nand_31 (nand_31_out, nand_27_out, Cin);
  nor nor_16 (nor_16_out, nor_10_out, nor_13_out);
  nor nor_17 (nor_17_out, nor_13_out, in_14);
  not nor_18 (nor_18_out, nor_10_out);  // NOR_Gate
  not nor_19 (nor_19_out, in_14);  // NOR_Gate
  nor nor_20 (nor_20_out, nor_12_out, nor_12_out);
  nor nor_21 (nor_21_out, nor_20_out, in_17);
  nand nand_32 (nand_32_out, nand_28_out, in_20);
  nand nand_33 (Carry_3, nand_31_out, nand_21_out);
  nor nor_22 (nor_22_out, nor_20_out, nor_21_out);
  nor nor_23 (nor_23_out, nor_21_out, in_17);
  nand nand_34 (nand_34_out, nand_28_out, nand_32_out);
  nand nand_35 (nand_35_out, nand_32_out, in_20, in_20);
  nor nor_24 (nor_24_out, A, nor_14_out);
  nor nor_25 (nor_25_out, nor_14_out, B_2);
  not nor_26 (nor_26_out, A);  // NOR_Gate
  not nor_27 (nor_27_out, B_2);  // NOR_Gate
  nor nor_28 (nor_28_out, A_3, nor_15_out);
  nor nor_29 (nor_29_out, nor_15_out, B_4);
  not nor_30 (nor_30_out, B_4);  // NOR_Gate
  nand nand_36 (nand_36_out, nand_27_out, nand_30_out);
  nand nand_37 (nand_37_out, nand_30_out, Cin, Cin);
  nor nor_31 (nor_31_out, nor_16_out, nor_17_out);
  nor nor_32 (nor_32_out, nor_18_out, nor_19_out);
  nor nor_33 (nor_33_out, nor_22_out, nor_23_out);
  nand nand_38 (Sum_3, nand_36_out, nand_37_out);
  nor nor_34 (Sum_4, nor_31_out, nor_31_out);
  nor nor_35 (nor_35_out, nor_32_out, nor_11_out);
  nor nor_36 (nor_36_out, nor_8_out, nor_22_out);
  nand nand_39 (Difference_4, nand_34_out, nand_35_out);
  nor nor_37 (nor_37_out, nor_24_out, nor_25_out);
  nor nor_38 (Carry_2, nor_26_out, nor_27_out);
  nor nor_39 (nor_39_out, nor_28_out, nor_29_out);
  nor nor_40 (Borrow_2, A_3, nor_30_out);
  not nor_41 (Carry_4, nor_35_out);  // NOR_Gate
  nor nor_42 (Difference_3, nor_36_out, nor_36_out);
  nor nor_43 (Borrow_3, nor_33_out, nor_33_out);
  nor nor_44 (Sum, nor_37_out, nor_37_out);
  nor nor_45 (Difference, nor_39_out, nor_39_out);

  // Notes on the sheet:
  //   Half Adder
  //   Half Subtractor
  //   Full Adder
  //   Full Subtractor
  //   A
  //   A
endmodule
