// Logisim project adder_shift.circ as structural Verilog: 1 circuit, main circuit main
module main (
  input  Shift,
  input  Clear,
  input  Input,
  input  Clear_2
);

  wire clock_1_out, d_ff_1_q, main_1_carry, main_1_sum, shift_register_1_out, shift_register_2_out, undriven,
       undriven_2;

  Clock clock_1 (.out(clock_1_out));
  Shift_Register shift_register_1 (
    .shift(Shift), .in(main_1_sum), .clk(clock_1_out), .out(shift_register_1_out), .clr(undriven));  // open: load, d0, q0, d1, q1, d2, q2, d3, q3, d4, q4, d5, q5, d6, q6, d7, q7
  Shift_Register shift_register_2 (
    .shift(Shift), .in(Input), .clk(clock_1_out), .out(shift_register_2_out), .clr(undriven_2));  // open: load, d0, q0, d1, q1, d2, q2, d3, q3, d4, q4, d5, q5, d6, q6, d7, q7
  full_adder_main main_1 (
    .A(shift_register_1_out), .B(shift_register_2_out), .Cin(d_ff_1_q), .Sum(main_1_sum), .Carry(main_1_carry));
  D_Flip_Flop d_ff_1 (.clk(clock_1_out), .D(main_1_carry), .Q(d_ff_1_q));  // open: Qn, preset, en, reset

  // Notes on the sheet:
  //   Clock
  //   Adder using Shift Register
endmodule
