// Logisim project als(1).circ as structural Verilog: 1 circuit, main circuit main
module main (
  input  Cin,
  input  [1:0] in_2,
  input  [1:0] in_3,
  output out_4,
  output out_5,
  output out_6,
  output out_7
);

  wire main_1_d0, main_1_d1, main_1_d2, main_1_d3, main_2_d0, main_2_d1, main_2_d2, main_2_d3,
       shift_register_1_q0, shift_register_1_q1, shift_register_1_q2, shift_register_1_q3,
       shift_register_2_q0, shift_register_2_q1, shift_register_2_q2, shift_register_2_q3;

  Shift_Register #(.length(4)) shift_register_1 (
    .q0(shift_register_1_q0), .q1(shift_register_1_q1), .q2(shift_register_1_q2), .q3(shift_register_1_q3));  // open: shift, in, clk, out, load, clr, d0, d1, d2, d3
  Shift_Register #(.length(4)) shift_register_2 (
    .q0(shift_register_2_q0), .q1(shift_register_2_q1), .q2(shift_register_2_q2), .q3(shift_register_2_q3));  // open: shift, in, clk, out, load, clr, d0, d1, d2, d3
  arithmetic_unit_main main_1 (
    .B3(shift_register_1_q0), .B2(shift_register_1_q1), .B1(shift_register_1_q2), .B0(shift_register_1_q3),
    .A3(shift_register_2_q0), .A2(shift_register_2_q1), .A1(shift_register_2_q2), .A0(shift_register_2_q3),
    .Cin(Cin), .Select(in_2), .D0(main_1_d0), .D1(main_1_d1), .D2(main_1_d2), .D3(main_1_d3));  // open: Cout
  logicunit_main main_2 (
    .B3(shift_register_1_q0), .B2(shift_register_1_q1), .B1(shift_register_1_q2), .B0(shift_register_1_q3),
    .A3(shift_register_2_q0), .A2(shift_register_2_q1), .A1(shift_register_2_q2), .A0(shift_register_2_q3),
    .Select(in_2), .D0(main_2_d0), .D1(main_2_d1), .D2(main_2_d2), .D3(main_2_d3));
  Multiplexer #(.select(2), .enable("false")) multiplexer_1 (
    .in0(main_1_d0), .in1(main_2_d0), .out(out_4), .sel(in_3));  // open: in2, in3
  Multiplexer #(.select(2), .enable("false")) multiplexer_2 (
    .in0(main_1_d1), .in1(main_2_d1), .out(out_5), .sel(in_3));  // open: in2, in3
  Multiplexer #(.select(2), .enable("false")) multiplexer_3 (
    .in0(main_1_d2), .in1(main_2_d2), .out(out_6), .sel(in_3));  // open: in2, in3
  Multiplexer #(.select(2), .enable("false")) multiplexer_4 (
    .in0(main_1_d3), .in1(main_2_d3), .out(out_7), .sel(in_3));  // open: in2, in3

  // Notes on the sheet:
  //   Arithmetic Logic Shift Unit
endmodule
