// Logisim project als.circ as structural Verilog: 1 circuit, main circuit main
module main (
  input  Cin,
  input  [3:0] in_2,
  input  [1:0] Select,
  input  [1:0] Select_Op,
  output out_5,
  output out_6,
  output out_7,
  output out_8
);

  wire clock_1_out, main_1_d0, main_1_d1, main_1_d2, main_1_d3, main_2_d0, main_2_d1, main_2_d2, main_2_d3,
       main_3_d0, main_3_d1, main_3_d2, main_3_d3, main_4_d0, main_4_d1, main_4_d2, main_4_d3,
       multiplexer_1_out, multiplexer_2_out, multiplexer_3_out, multiplexer_4_out, Register_A_q0,
       Register_A_q1, Register_A_q2, Register_A_q3, Register_B_q0, Register_B_q1, Register_B_q2,
       Register_B_q3;

  Shift_Register #(.length(4)) Register_B (
    .q0(Register_B_q0), .q1(Register_B_q1), .q2(Register_B_q2), .q3(Register_B_q3));  // open: shift, in, clk, out, load, clr, d0, d1, d2, d3
  Shift_Register #(.length(4)) Register_A (
    .clk(clock_1_out), .d0(out_5), .q0(Register_A_q0), .d1(out_6), .q1(Register_A_q1), .d2(out_7),
    .q2(Register_A_q2), .d3(out_8), .q3(Register_A_q3));  // open: shift, in, out, load, clr
  arithmetic_unit_main main_1 (
    .B3(Register_B_q0), .B2(Register_B_q1), .B1(Register_B_q2), .B0(Register_B_q3), .A3(Register_A_q0),
    .A2(Register_A_q1), .A1(Register_A_q2), .A0(Register_A_q3), .Cin(Cin), .Select(Select), .D0(main_1_d0),
    .D1(main_1_d1), .D2(main_1_d2), .D3(main_1_d3));  // open: Cout
  logicunit_main main_2 (
    .B3(Register_B_q0), .B2(Register_B_q1), .B1(Register_B_q2), .B0(Register_B_q3), .A3(Register_A_q0),
    .A2(Register_A_q1), .A1(Register_A_q2), .A0(Register_A_q3), .Select(Select), .D0(main_2_d0),
    .D1(main_2_d1), .D2(main_2_d2), .D3(main_2_d3));
  shift_unit_main main_3 (
    .SelectShift(Select), .A3(Register_A_q0), .A2(Register_A_q1), .A1(Register_A_q2), .A0(Register_A_q3),
    .SelectLR(1'b1), .D0(main_3_d0), .D1(main_3_d1), .D2(main_3_d2), .D3(main_3_d3));
  shift_unit_main main_4 (
    .SelectShift(Select), .A3(Register_A_q0), .A2(Register_A_q1), .A1(Register_A_q2), .A0(Register_A_q3),
    .SelectLR(1'b0), .D0(main_4_d0), .D1(main_4_d1), .D2(main_4_d2), .D3(main_4_d3));
  Multiplexer #(.select(2), .enable("false")) multiplexer_1 (
    .in0(main_1_d0), .in1(main_2_d0), .in2(main_3_d0), .in3(main_4_d0), .out(multiplexer_1_out),
    .sel(Select_Op));
  Multiplexer #(.select(2), .enable("false")) multiplexer_2 (
    .in0(main_1_d1), .in1(main_2_d1), .in2(main_3_d1), .in3(main_4_d1), .out(multiplexer_2_out),
    .sel(Select_Op));
  Multiplexer #(.select(2), .enable("false")) multiplexer_3 (
    .in0(main_1_d2), .in1(main_2_d2), .in2(main_3_d2), .in3(main_4_d2), .out(multiplexer_3_out),
    .sel(Select_Op));
  Multiplexer #(.select(2), .enable("false")) multiplexer_4 (
    .in0(main_1_d3), .in1(main_2_d3), .in2(main_3_d3), .in3(main_4_d3), .out(multiplexer_4_out),
    .sel(Select_Op));
  Register #(.width(1)) register_1 (.D(multiplexer_1_out), .Q(out_8), .clk(clock_1_out));  // open: en, clr
  Register #(.width(1)) register_2 (.D(multiplexer_2_out), .Q(out_7), .clk(clock_1_out));  // open: en, clr
  Register #(.width(1)) register_3 (.D(multiplexer_3_out), .Q(out_6), .clk(clock_1_out));  // open: en, clr
  Register #(.width(1)) register_4 (.D(multiplexer_4_out), .Q(out_5), .clk(clock_1_out));  // open: en, clr
  Clock clock_1 (.out(clock_1_out));

  // Notes on the sheet:
  //   Arithmetic Logic Shift Unit
endmodule
