// Logisim project bidirect_shiftregister.circ as structural Verilog: 1 circuit, main circuit main
module main (
  input  Clear,
  input  Input,
  input  Input_2,
  input  Select
);

  wire and_1_out, and_2_out, and_3_out, and_4_out, and_5_out, and_6_out, and_7_out, and_8_out, clock_1_out,
       d_ff_1_q, d_ff_2_q, d_ff_3_q, d_ff_4_q, not_1_out, or_1_out, or_2_out, or_3_out, or_4_out;

  Clock clock_1 (.out(clock_1_out));
  or or_1 (or_1_out, and_1_out, and_2_out);
  and and_1 (and_1_out, Input, Select);
  and and_2 (and_2_out, not_1_out, d_ff_2_q);
  not not_1 (not_1_out, Select);
  D_Flip_Flop d_ff_1 (.clk(clock_1_out), .D(or_1_out), .Q(d_ff_1_q), .reset(Clear));  // open: Qn, preset, en
  or or_2 (or_2_out, and_3_out, and_5_out);
  and and_3 (and_3_out, d_ff_1_q, Select);
  D_Flip_Flop d_ff_2 (.clk(clock_1_out), .D(or_2_out), .Q(d_ff_2_q), .reset(Clear));  // open: Qn, preset, en
  and and_4 (and_4_out, d_ff_2_q, Select);
  and and_5 (and_5_out, not_1_out, d_ff_3_q);
  D_Flip_Flop d_ff_3 (.clk(clock_1_out), .D(or_3_out), .Q(d_ff_3_q), .reset(Clear));  // open: Qn, preset, en
  or or_3 (or_3_out, and_4_out, and_6_out);
  and and_6 (and_6_out, not_1_out, d_ff_4_q);
  or or_4 (or_4_out, and_7_out, and_8_out);
  and and_7 (and_7_out, d_ff_3_q, Select);
  and and_8 (and_8_out, not_1_out, Input_2);
  D_Flip_Flop d_ff_4 (.clk(clock_1_out), .D(or_4_out), .Q(d_ff_4_q), .reset(Clear));  // open: Qn, preset, en

  // Notes on the sheet:
  //   Clock
  //   Bidirectional Shift Register
endmodule
