// Logisim project common_bus_system_14bce110.circ as structural Verilog: 1 circuit, main circuit main
module main (
  input  [1:0] in_1,
  output out_2,
  output out_3,
  output out_4,
  output out_5
);

  wire clock_1_out, shift_register_1_q0, shift_register_1_q1, shift_register_1_q2, shift_register_1_q3,
       shift_register_2_q0, shift_register_2_q1, shift_register_2_q2, shift_register_2_q3,
       shift_register_3_q0, shift_register_3_q1, shift_register_3_q2, shift_register_3_q3,
       shift_register_4_q0, shift_register_4_q1, shift_register_4_q2, shift_register_4_q3;

  Clock clock_1 (.out(clock_1_out));
  Shift_Register #(.length(4)) shift_register_1 (
    .clk(clock_1_out), .q0(shift_register_1_q0), .q1(shift_register_1_q1), .q2(shift_register_1_q2),
    .q3(shift_register_1_q3));  // open: shift, in, out, load, clr, d0, d1, d2, d3
  Multiplexer #(.select(2), .enable("false")) multiplexer_1 (
    .in0(shift_register_1_q0), .in1(shift_register_2_q0), .in2(shift_register_3_q0),
    .in3(shift_register_4_q0), .out(out_2), .sel(in_1));
  Shift_Register #(.length(4)) shift_register_2 (
    .clk(clock_1_out), .q0(shift_register_2_q0), .q1(shift_register_2_q1), .q2(shift_register_2_q2),
    .q3(shift_register_2_q3));  // open: shift, in, out, load, clr, d0, d1, d2, d3
  Multiplexer #(.select(2), .enable("false")) multiplexer_2 (
    .in0(shift_register_1_q1), .in1(shift_register_2_q1), .in2(shift_register_3_q1),
    .in3(shift_register_4_q1), .out(out_3), .sel(in_1));
  Shift_Register #(.length(4)) shift_register_3 (
    .clk(clock_1_out), .q0(shift_register_3_q0), .q1(shift_register_3_q1), .q2(shift_register_3_q2),
    .q3(shift_register_3_q3));  // open: shift, in, out, load, clr, d0, d1, d2, d3
  Shift_Register #(.length(4)) shift_register_4 (
    .clk(clock_1_out), .q0(shift_register_4_q0), .q1(shift_register_4_q1), .q2(shift_register_4_q2),
    .q3(shift_register_4_q3));  // open: shift, in, out, load, clr, d0, d1, d2, d3
  Multiplexer #(.select(2), .enable("false")) multiplexer_3 (
    .in0(shift_register_1_q2), .in1(shift_register_2_q2), .in2(shift_register_3_q2),
    .in3(shift_register_4_q2), .out(out_4), .sel(in_1));
  Multiplexer #(.select(2), .enable("false")) multiplexer_4 (
    .in0(shift_register_1_q3), .in1(shift_register_2_q3), .in2(shift_register_3_q3),
    .in3(shift_register_4_q3), .out(out_5), .sel(in_1));

  // Notes on the sheet:
  //   Common Bus System for 4 Registers
endmodule
