// Logisim project common_bus_system_serial_14bce110.circ as structural Verilog: 1 circuit, main circuit main
module main (
  input  [3:0] in_1,
  input  [1:0] in_2,
  input  [3:0] in_3,
  input  [3:0] in_4,
  input  [3:0] in_5,
  input  [3:0] in_6
);

  wire clock_1_out;
  wire [3:0] register_1_q, register_2_q, register_3_q, register_4_q;

  Clock clock_1 (.out(clock_1_out));
  Register #(.width(4)) register_1 (.D(in_3), .Q(register_1_q), .clk(clock_1_out));  // open: en, clr
  Register #(.width(4)) register_2 (.D(in_4), .Q(register_2_q), .clk(clock_1_out));  // open: en, clr
  Multiplexer #(.select(2), .width(4)) multiplexer_1 (
    .in0(register_1_q), .in1(register_2_q), .in2(register_3_q), .in3(register_4_q), .out(in_1), .sel(in_2),
    .en(1'b1));
  Register #(.width(4)) register_3 (.D(in_5), .Q(register_3_q), .clk(clock_1_out));  // open: en, clr
  Register #(.width(4)) register_4 (.D(in_6), .Q(register_4_q), .clk(clock_1_out));  // open: en, clr

  // Notes on the sheet:
  //   Common Bus System with Serial Input
endmodule
