// Logisim project full adder.circ as structural Verilog: 1 circuit, main circuit main
module main (
  input  A,
  input  B,
  input  Cin,
  output Sum,
  output Carry
);

  wire nand_1_out, nand_2_out, nand_3_out, nand_4_out, nand_5_out, nand_6_out, nand_7_out, nand_8_out,
       nand_9_out;

  nand nand_1 (nand_1_out, A, B);
  nand nand_2 (nand_2_out, A, nand_1_out);
  nand nand_3 (nand_3_out, nand_1_out, B, B);
  nand nand_4 (nand_4_out, A, B);
  nand nand_5 (nand_5_out, nand_2_out, nand_3_out);
  nand nand_6 (nand_6_out, nand_5_out, Cin);
  nand nand_7 (nand_7_out, nand_5_out, Cin);
  nand nand_8 (nand_8_out, nand_5_out, nand_7_out);
  nand nand_9 (nand_9_out, nand_7_out, Cin, Cin);
  nand nand_10 (Carry, nand_6_out, nand_4_out);
  nand nand_11 (Sum, nand_8_out, nand_9_out);

  // Notes on the sheet:
  //   A
endmodule
