// Logisim project incr_dec.circ as structural Verilog: 1 circuit, main circuit main
module main (
  input  in_1,
  input  in_2,
  input  in_3,
  input  in_4,
  output out_5,
  output out_6,
  output out_7,
  output out_8,
  output out_9
);

  wire main_2_carry, main_3_carry, main_4_carry, multiplexer_1_out, multiplexer_2_out, multiplexer_3_out,
       multiplexer_4_out, shift_register_1_q0, shift_register_1_q1, shift_register_1_q2, shift_register_1_q3;

  Multiplexer #(.enable("false")) multiplexer_1 (.in0(in_4), .in1(in_3), .out(multiplexer_1_out), .sel(in_2));
  Shift_Register #(.length(4)) shift_register_1 (
    .q0(shift_register_1_q0), .q1(shift_register_1_q1), .q2(shift_register_1_q2), .q3(shift_register_1_q3));  // open: shift, in, clk, out, load, clr, d0, d1, d2, d3
  Multiplexer #(.enable("false")) multiplexer_2 (.in0(in_4), .in1(in_3), .out(multiplexer_2_out), .sel(in_2));
  Multiplexer #(.enable("false")) multiplexer_3 (.in0(in_4), .in1(in_3), .out(multiplexer_3_out), .sel(in_2));
  Multiplexer #(.enable("false")) multiplexer_4 (.in0(in_4), .in1(in_4), .out(multiplexer_4_out), .sel(in_2));
  full_adder_main main_1 (
    .A(shift_register_1_q0), .B(multiplexer_1_out), .Cin(main_2_carry), .Sum(out_5), .Carry(out_9));
  full_adder_main main_2 (
    .A(shift_register_1_q1), .B(multiplexer_3_out), .Cin(main_3_carry), .Sum(out_6), .Carry(main_2_carry));
  full_adder_main main_3 (
    .A(shift_register_1_q2), .B(multiplexer_2_out), .Cin(main_4_carry), .Sum(out_7), .Carry(main_3_carry));
  full_adder_main main_4 (
    .A(shift_register_1_q3), .B(multiplexer_4_out), .Cin(in_1), .Sum(out_8), .Carry(main_4_carry));

  // Notes on the sheet:
  //   Increment/Decrement
endmodule
