// Logisim project logicunit.circ as structural Verilog: 1 circuit, main circuit main
module main (
  input  B3,
  input  B2,
  input  B1,
  input  B0,
  input  A3,
  input  A2,
  input  A1,
  input  A0,
  input  [1:0] Select,
  output D0,
  output D1,
  output D2,
  output D3
);

  wire and_1_out, and_2_out, and_3_out, and_4_out, not_1_out, not_2_out, not_3_out, not_4_out, or_1_out,
       or_2_out, or_3_out, or_4_out, xor_1_out, xor_2_out, xor_3_out, xor_4_out;

  and and_1 (and_1_out, A0, B0);
  or or_1 (or_1_out, A0, B0);
  xor xor_1 (xor_1_out, A0, B0);
  not not_1 (not_1_out, A0);
  and and_2 (and_2_out, A1, B1);
  or or_2 (or_2_out, A1, B1);
  xor xor_2 (xor_2_out, A1, B1);
  not not_2 (not_2_out, A1);
  and and_3 (and_3_out, A2, B2);
  or or_3 (or_3_out, A2, B2);
  xor xor_3 (xor_3_out, A2, B2);
  not not_3 (not_3_out, A2);
  and and_4 (and_4_out, A3, B3);
  or or_4 (or_4_out, A3, B3);
  xor xor_4 (xor_4_out, A3, B3);
  not not_4 (not_4_out, A3);
  Multiplexer #(.select(2), .enable("false")) multiplexer_1 (
    .in0(and_1_out), .in1(or_1_out), .in2(xor_1_out), .in3(not_1_out), .out(D0), .sel(Select));
  Multiplexer #(.select(2), .enable("false")) multiplexer_2 (
    .in0(and_2_out), .in1(or_2_out), .in2(xor_2_out), .in3(not_2_out), .out(D1), .sel(Select));
  Multiplexer #(.select(2), .enable("false")) multiplexer_3 (
    .in0(and_3_out), .in1(or_3_out), .in2(xor_3_out), .in3(not_3_out), .out(D2), .sel(Select));
  Multiplexer #(.select(2), .enable("false")) multiplexer_4 (
    .in0(and_4_out), .in1(or_4_out), .in2(xor_4_out), .in3(not_4_out), .out(D3), .sel(Select));

  // Notes on the sheet:
  //   Logic Unit
endmodule
