// Logisim project shift_unit.circ as structural Verilog: 1 circuit, main circuit main
module main (
  input  A3,
  input  A2,
  input  A1,
  input  A0,
  input  SelectLR,
  input  [1:0] SelectShift,
  output D0,
  output D1,
  output D2,
  output D3
);

  wire multiplexer_1_out, multiplexer_2_out, multiplexer_3_out;

  Multiplexer #(.select(2), .enable("false")) multiplexer_1 (
    .in0(A2), .in1(A2), .in2(A3), .in3(A2), .out(multiplexer_1_out), .sel(SelectShift));
  Multiplexer #(.select(2), .enable("false")) multiplexer_2 (
    .in0(1'b0), .in1(A3), .in2(1'b0), .in3(1'b0), .out(multiplexer_2_out), .sel(SelectShift));
  Multiplexer #(.select(2), .enable("false")) multiplexer_3 (
    .in0(1'b0), .in1(A0), .in2(A3), .in3(1'b0), .out(multiplexer_3_out), .sel(SelectShift));
  Multiplexer #(.enable("false")) multiplexer_4 (.in0(multiplexer_2_out), .in1(A1), .out(D0), .sel(SelectLR));
  Multiplexer #(.enable("false")) multiplexer_5 (.in0(A0), .in1(A2), .out(D1), .sel(SelectLR));
  Multiplexer #(.enable("false")) multiplexer_6 (.in0(A1), .in1(A3), .out(D2), .sel(SelectLR));
  Multiplexer #(.enable("false")) multiplexer_7 (
    .in0(multiplexer_1_out), .in1(multiplexer_3_out), .out(D3), .sel(SelectLR));

  // Notes on the sheet:
  //   Shift Unit
endmodule
