// Logisim project subtractor_shift.circ as structural Verilog: 1 circuit, main circuit main
module main (
  input  in_1,
  input  Clear,
  input  Input,
  input  Clear_2
);

  wire clock_1_out, d_ff_1_q, main_1_borrow, main_1_difference, shift_register_1_out, shift_register_2_out,
       undriven, undriven_2;

  Clock clock_1 (.out(clock_1_out));
  Shift_Register shift_register_1 (
    .shift(in_1), .in(main_1_difference), .clk(clock_1_out), .out(shift_register_1_out), .clr(undriven));  // open: load, d0, q0, d1, q1, d2, q2, d3, q3, d4, q4, d5, q5, d6, q6, d7, q7
  Shift_Register shift_register_2 (
    .shift(in_1), .in(Input), .clk(clock_1_out), .out(shift_register_2_out), .clr(undriven_2));  // open: load, d0, q0, d1, q1, d2, q2, d3, q3, d4, q4, d5, q5, d6, q6, d7, q7
  full_subtractor_main main_1 (
    .A(shift_register_1_out), .B(shift_register_2_out), .in_3(d_ff_1_q), .Difference(main_1_difference),
    .Borrow(main_1_borrow));
  D_Flip_Flop d_ff_1 (.clk(clock_1_out), .D(main_1_borrow), .Q(d_ff_1_q));  // open: Qn, preset, en, reset

  // Notes on the sheet:
  //   Clock
  //   Subtractor using Shift Register
endmodule
