// Logisim project universal_shift_register.circ as structural Verilog: 1 circuit, main circuit main
module main (
  input  [1:0] Select,
  input  in_2,
  input  in_3,
  input  I3,
  input  I2,
  input  I1,
  input  I0,
  output A3,
  output A2,
  output A1,
  output A0
);

  wire clock_1_out, multiplexer_1_out, multiplexer_2_out, multiplexer_3_out, multiplexer_4_out;

  Clock clock_1 (.out(clock_1_out));
  Multiplexer #(.select(2), .enable("false")) multiplexer_1 (
    .in0(I3), .in1(A2), .in2(in_3), .in3(A3), .out(multiplexer_1_out), .sel(Select));
  D_Flip_Flop d_ff_1 (.clk(clock_1_out), .D(multiplexer_1_out), .Q(A3));  // open: Qn, preset, en, reset
  D_Flip_Flop d_ff_2 (.clk(clock_1_out), .D(multiplexer_2_out), .Q(A2));  // open: Qn, preset, en, reset
  Multiplexer #(.select(2), .enable("false")) multiplexer_2 (
    .in0(I2), .in1(A1), .in2(A3), .in3(A2), .out(multiplexer_2_out), .sel(Select));
  Multiplexer #(.select(2), .enable("false")) multiplexer_3 (
    .in0(I1), .in1(A0), .in2(A2), .in3(A1), .out(multiplexer_3_out), .sel(Select));
  D_Flip_Flop d_ff_3 (.clk(clock_1_out), .D(multiplexer_3_out), .Q(A1));  // open: Qn, preset, en, reset
  D_Flip_Flop d_ff_4 (.clk(clock_1_out), .D(multiplexer_4_out), .Q(A0));  // open: Qn, preset, en, reset
  Multiplexer #(.select(2), .enable("false")) multiplexer_4 (
    .in0(I0), .in1(in_2), .in2(A1), .in3(A0), .out(multiplexer_4_out), .sel(Select));

  // Notes on the sheet:
  //   Clock
  //   Serial Input for Shift Right
  //   Universal Shift Register
  //   Serial Input for Shift Left
endmodule
